// Digital circuit reg4-tri.dig as structural Verilog
module reg4_tri (
  input  Write,
  input  Read,
  input  d_3,
  input  d_2,
  input  d_1,
  input  d_0
);

  wire d_ff_1_q, d_ff_2_q, d_ff_3_q, d_ff_4_q;

  D_FF d_ff_1 (.D(d_3), .C(Write), .Q(d_ff_1_q));  // open: nQ
  assign d_3 = Read ? d_ff_1_q : 1'bz;  // Driver driver_1
  D_FF d_ff_2 (.D(d_2), .C(Write), .Q(d_ff_2_q));  // open: nQ
  assign d_2 = Read ? d_ff_2_q : 1'bz;  // Driver driver_2
  D_FF d_ff_3 (.D(d_1), .C(Write), .Q(d_ff_3_q));  // open: nQ
  assign d_1 = Read ? d_ff_3_q : 1'bz;  // Driver driver_3
  D_FF d_ff_4 (.D(d_0), .C(Write), .Q(d_ff_4_q));  // open: nQ
  assign d_0 = Read ? d_ff_4_q : 1'bz;  // Driver driver_4

  // Notes on the sheet:
  //   Write: Coge los datos de el bus y lo guarda en el sitio al que este conectado.
  //   Read: Lee los valores de a lo que se suponga que este conectado, y transmite los mismos al bus.
endmodule
